// Logisim project ex5.circ as structural Verilog: 5 circuits, main circuit rotr
module rotr (
  input  [15:0] A,
  input  [3:0] B,
  output [15:0] Out1,
  output [15:0] out_4,
  output [15:0] out_5,
  output [15:0] out_6,
  output [15:0] out_7
);

  wire [15:0] rot1_1_out_2, rot2_1_out_2, rot4_1_out_2, rot8_1_out_2;

  Multiplexer #(.enable("false"), .width(16)) multiplexer_1 (.in0(A), .in1(rot1_1_out_2), .out(out_5), .sel(B[0]));
  rot1 rot1_1 (.in_1(A), .out_2(rot1_1_out_2));
  Multiplexer #(.enable("false"), .width(16)) multiplexer_2 (.in0(out_5), .in1(rot2_1_out_2), .out(out_6), .sel(B[1]));
  rot2 rot2_1 (.in_1(out_5), .out_2(rot2_1_out_2));
  Multiplexer #(.enable("false"), .width(16)) multiplexer_3 (.in0(out_6), .in1(rot4_1_out_2), .out(out_4), .sel(B[2]));
  rot4 rot4_1 (.in_1(out_6), .out_2(rot4_1_out_2));
  Multiplexer #(.enable("false"), .width(16)) multiplexer_4 (.in0(out_4), .in1(rot8_1_out_2), .out(Out1), .sel(B[3]));
  rot8 rot8_1 (.in_1(out_4), .out_2(rot8_1_out_2));

  assign out_7 = Out1;

  // Other names for the same wires on the sheet: s0 = B[0]; s1 = B[1]; s2 = B[2]; s3 = B[3]; input1[15:0] = A;
  //   input2[15:0] = out_5; input3[15:0] = out_6; input4[15:0] = out_4; input5[15:0] = Out1

  // Notes on the sheet:
  //   PUT CIRCUITRY HERE
endmodule

module rot8 (
  input  [15:0] in_1,
  output [15:0] out_2
);


  assign out_2 = {in_1[7:0], in_1[15:8]};

  // Other names for the same wires on the sheet: d8to15[7:0] = in_1[15:8]; d0to7[7:0] = in_1[7:0]

  // Notes on the sheet:
  //   PUT CIRCUITRY HERE
endmodule

module rot4 (
  input  [15:0] in_1,
  output [15:0] out_2
);


  assign out_2 = {in_1[3:0], in_1[15:4]};

  // Other names for the same wires on the sheet: d4to15[11:0] = in_1[15:4]; d0to3[3:0] = in_1[3:0]

  // Notes on the sheet:
  //   PUT CIRCUITRY HERE
endmodule

module rot2 (
  input  [15:0] in_1,
  output [15:0] out_2
);


  assign out_2 = {in_1[1:0], in_1[15:2]};

  // Other names for the same wires on the sheet: d2to15[13:0] = in_1[15:2]; d0to1[1:0] = in_1[1:0]

  // Notes on the sheet:
  //   PUT CIRCUITRY HERE
endmodule

module rot1 (
  input  [15:0] in_1,
  output [15:0] out_2
);


  assign out_2 = {in_1[0], in_1[15:1]};

  // Other names for the same wires on the sheet: d1to15[14:0] = in_1[15:1]; d0 = in_1[0]

  // Notes on the sheet:
  //   PUT CIRCUITRY HERE
endmodule
